# Fritzing sketch AlarDuino (saved by Fritzing 0.9.0b)
circuit board: 6.88566cm x 5.36311cm
breadboards: 1

parts:
  ADXL = ADXL335 Accelerometer Breakout
  TMP = TMP36 Temperature Sensor [package="TO92 [THT]"]
  JCK1 = Audio Jack (TRS) 3.5mm [package="4Ucon 08780 [THT]"]
  JCK2 = Audio Jack (TRS) 3.5mm [package="4Ucon 08780 [THT]"]
  NPN = NPN-Transistor [package="TO92 [THT]"]
  R1 = Resistor [tolerance=±5% resistance=1.5k package=THT]
  LED = LED - 5mm [color="Red (633nm)" package="5 mm [THT]"]
  R2 = Resistor [tolerance=±5% resistance=220 package=THT]
  J8 = rounded female pin header, 10 pins [form="♀ (female rounded)"]
  J9 = rounded female pin header, 8 pins [form="♀ (female rounded)"]  # not connected
  J10 = rounded female pin header, 8 pins [form="♀ (female rounded)"]
  J11 = rounded female pin header, 6 pins [form="♀ (female rounded)"]
  BAT = Battery
  C1 = Ceramic Capacitor [capacitance=10nF package="100 mil [THT, multilayer]"]
  BRL = Power plug
  C2 = Electrolytic Capacitor [capacitance=10µF package="100 mil [THT, electrolytic]"]
  POT1_(tmp) = Breadboard Trimpot
  POT2_(acc) = Breadboard Trimpot
  D1 = Diode [package=diode-1n4001]
  SG3 = Buzzer 12mm [package=buzzer-12mm-ns-kit]
  RST = Pushbutton [package="[THT]"]

nets:
  5V: ADXL.Vin, TMP.+Vs, JCK2.Tip, J10.pin5, C2.+, POT1_(tmp).PIN1, POT2_(acc).PIN1
  GND: ADXL.GND, TMP.GND, JCK2.Sleeve, LED.cathode, J8.pin4, J10.pin6, C1.1, C2.-, POT1_(tmp).PIN3, POT2_(acc).PIN3, SG3.2, RST.Pin_3
  N1: ADXL.Xout, J11.pin5
  N2: ADXL.Yout, J11.pin4
  N3: ADXL.Zout, J11.pin3
  N4: TMP.Vout, J11.pin1, C1.0
  N5: JCK1.Sleeve, NPN.C
  N6: JCK1.Ring, JCK1.Tip, BRL.VCC, D1.C
  N7: JCK2.Ring, J8.pin6
  N8: NPN.E, BAT.-, BRL.GND
  N9: NPN.B, R1.Pin_1
  N10: R1.Pin_0, J8.pin8
  N11: LED.anode, R2.Pin_0
  N12: R2.Pin_1, J8.pin9
  N13: J8.pin7, SG3.1
  N14: J10.pin3, RST.Pin_1, RST.Pin_2
  N15: J11.pin2, POT1_(tmp).PIN2
  N16: J11.pin6, POT2_(acc).PIN2
  N17: BAT.+, D1.A

notes:
  PIR
  SRN
  4
  ALARDUINO
  by PAKOZM
  GND
  5V
  5APOT
  ~5
  VCC
  2016 v0.1
  ~11
  SIREN
  TMP
  0TMP
  2Z0
  3Y0
  4X0
  13
  12
  RX<-0
  TX->1
  ~3
  ~6
  ~10
  ~9
  7
  AREF
  LED
  BUZ
  Sound Bomb1 - Twin Piezo elements
  110dB sound output
  Only 85mA current consumption
  Compact ABS enclosure in white
  Twin wall fixing lugs
  15cm flying lead ( Black & Red)
  12VDC Powered
  http://www.w9xt.com/page_microdesign_pt7_transistor_switching.html
  hFE = 35 (worst case)
  Is = 85 (siren current)
  Ib = 85/35 = 2.5 => 3mA room
  VBE(sat) = 1V
  VP0 = 5V
  VP0 = VR1 + VBE
  VR1 = VP0 - VBE = 5 - 1 = 4V
  R = VR1/Ib = 4/0.003 = 1333
  12V
  2
  8
  GND LOOP
  A1
  1TPOT
  AlarDuino, Car Alarm Arduino Shield, 0.1
  RST
  max=18
  max=8C
  Vin
  3.3V

custom parts:
  ADXL335 Accelerometer Breakout: ADXL335 Accelerometer Breakout board
