# Fritzing sketch RXShield (saved by Fritzing 0.9.0b)
circuit board: 6.88566cm x 5.36311cm
breadboards: 1

parts:
  PROGRAM = Pushbutton [package="[THT]"]
  RESET = Pushbutton [package="[THT]"]
  RX = female pin header, 4 pins [form="♀ (female)"]
  Attiny85 = attiny85 [package=dip]
  VCC = female pin header, 3 pins [form="♀ (female)"]
  10uF = Electrolytic Capacitor [capacitance=10µF package="100 mil [THT, electrolytic]"]
  1K = Resistor [tolerance=±5% resistance=1k package=THT]
  10uF_2 = Electrolytic Capacitor [capacitance=10µF package="100 mil [THT, electrolytic]"]
  D1 = Rectifier Diode [part_number=1N4001 package="300 mil [THT]"]
  D2 = Rectifier Diode [part_number=1N4001 package="300 mil [THT]"]
  D3 = Rectifier Diode [part_number=1N4001 package="300 mil [THT]"]
  47K = Resistor [tolerance=±5% resistance=47k package=THT]
  22K = Resistor [tolerance=±5% resistance=22k package=THT]
  LED1 = LED - 5mm [color="Red (633nm)" package="5 mm [THT]"]
  1K_2 = Resistor [tolerance=±5% resistance=1k package=THT]
  3V3 = Voltage Regulator - 3.3V [package="TO220 [THT]"]
  10uF_3 = Electrolytic Capacitor [capacitance=10µF package="100 mil [THT, electrolytic]"]
  REG = female pin header, 2 pins [form="♀ (female)"]
  J14 = rounded female pin header, 10 pins [form="♀ (female rounded)"]
  J15 = rounded female pin header, 8 pins [form="♀ (female rounded)"]
  J16 = rounded female pin header, 6 pins [form="♀ (female rounded)"]  # not connected
  J17 = rounded female pin header, 8 pins [form="♀ (female rounded)"]

nets:
  N1: PROGRAM.Pin_1, PROGRAM.Pin_2, J15.pin5
  GND: PROGRAM.Pin_3, PROGRAM.Pin_4, RESET.Pin_3, RESET.Pin_4, RX.pin1, Attiny85.Pin_4, 10uF.-, 10uF_2.-, 47K.Pin_0, LED1.cathode, 3V3.GND, 10uF_3.-, J14.pin4, J17.pin6
  RESET: RESET.Pin_1, RESET.Pin_2, Attiny85.Pin_1, J17.pin3
  N2: RX.pin3, 1K.Pin_1
  5V: RX.pin4, 10uF_2.+, D1.anode, 3V3.input_voltage, 10uF_3.+, J17.pin5
  N3: Attiny85.Pin_3, 1K_2.Pin_1
  N4: Attiny85.Pin_5, 47K.Pin_1, 22K.Pin_1
  N5: Attiny85.Pin_6, J14.pin10
  N6: Attiny85.Pin_7, 1K.Pin_0
  VOUT: Attiny85.Pin_8, VCC.pin2, 10uF.+, REG.pin2
  N7: VCC.pin1, D3.cathode
  N8: VCC.pin3, J17.pin4
  N9: D1.cathode, D2.anode
  N10: D2.cathode, D3.anode
  N11: 22K.Pin_0, J15.pin1
  N12: LED1.anode, 1K_2.Pin_0
  N13: 3V3.output_voltage, REG.pin1

notes:
  GND
  OUT
  VCC
  3V
  3V3
  ACK:
  CMD:
  PRG:
  RX RECEIVER v0.1
  PAKOZM (2016)
  13
  12
  ~11
  RX<-0
  TX->1
  2
  ~3
  4
  ~5
  ~6
  ~10
  ~9
  8
  7
  AREF
  Rst
  Vin
  A5
  A1
  A0
  A2
  A3
  A4
  5V
  SDA
  SCL
  RXShiled, Shield for RX 433 MHz receiver using Attiny85, 0.1
